# Fritzing sketch HMI_Relays (saved by Fritzing 0.9.3b)

parts:
  Part1 = Arduino Uno (Rev3)
  Part2 = Adafruit Micro USB Breakout [part_number="Adafruit #1833"]
  U2 = 4-Channel 5v Relay Shield [package=relay-4ch5v10a]
  Part3 = Nextion LCD DRAFT [part_number=Nextion]

nets:
  N1: Part1.D8, U2.IN1
  N2: Part1.D9_PWM, U2.IN2
  N3: Part1.D10_PWM/SS, U2.IN3
  N4: Part1.D11_PWM/MOSI, U2.IN4
  N5: Part1.D0/RX, Part3.Tx
  N6: Part1.D1/TX, Part3.Rx
  VCC: Part1.5V, Part2.VBUS, U2.VCC, Part3.VCC
  GND: Part1.GND, Part2.GND, U2.GND, Part3.GND

notes:
  HMI CONTROLS 4 RELAYS  WITH ARDUINO UNO
  USB 5V
  RELAY 4 CHANNEL
  ARDUINO UNO
  NEXTION HMI

custom parts:
  Adafruit Micro USB Breakout: Simple but effective - this breakout board has a USB Micro-B connector, with all 5 pins broken out. Great for pairing with a microcontroller with USB support, or adding USB 5V power to a project. We use a micro-AB connector with through-hole shielding pads for an excellent strong connection - it won't rip off by accident! Comes with one fully assembled and tested micro B breakout PCB and a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
  4-Channel 5v Relay Shield: 4 Channel 5v Relay Shield w. 2x SPD-06VDC-SD-C
  Nextion LCD DRAFT: Nextion HMI 2.4" TFT 320x240 resistive Lcd touch screen Intelligent Display Module for Arduino NX3224T024 4M Flash, 2KByte RAM, 65k colors
